// Logisim project assn_1.circ as structural Verilog: 2 circuits, main circuit main
module ALU_1_bit (
  input  Cin,
  input  A,
  input  B,
  input  Add_0_And_1,
  output Output,
  output Cout
);

  wire adder_1_out, and_1_out;

  Adder #(.width(1)) adder_1 (.a(A), .b(B), .out(adder_1_out), .cin(Cin), .cout(Cout));
  and and_1 (and_1_out, A, B);
  Multiplexer #(.enable("false")) multiplexer_1 (.in0(adder_1_out), .in1(and_1_out), .out(Output), .sel(Add_0_And_1));
endmodule

module main (
  input  in_1,
  input  [3:0] in_2,
  input  [3:0] in_3,
  input  in_4,
  output [3:0] out_5,
  output out_6
);

  wire alu_1_bit_1_cout, alu_1_bit_2_cout, alu_1_bit_3_cout;

  ALU_1_bit alu_1_bit_1 (
    .Cin(in_1), .A(in_2[0]), .Output(out_5[0]), .B(in_3[0]), .Add_0_And_1(in_4), .Cout(alu_1_bit_1_cout));
  ALU_1_bit alu_1_bit_2 (
    .Cin(alu_1_bit_1_cout), .A(in_2[1]), .Output(out_5[1]), .B(in_3[1]), .Add_0_And_1(in_4),
    .Cout(alu_1_bit_2_cout));
  ALU_1_bit alu_1_bit_3 (
    .Cin(alu_1_bit_2_cout), .A(in_2[2]), .Output(out_5[2]), .B(in_3[2]), .Add_0_And_1(in_4),
    .Cout(alu_1_bit_3_cout));
  ALU_1_bit alu_1_bit_4 (
    .Cin(alu_1_bit_3_cout), .A(in_2[3]), .Output(out_5[3]), .B(in_3[3]), .Add_0_And_1(in_4), .Cout(out_6));
endmodule
